// Digital circuit InstructionDecoder.dig as structural Verilog
// The InstructionDecoder component, which serves as a hub to control many of the signals to other components. It implements both the fetch operation, and execution of machine code (including decoding).
module InstructionDecoder (
  input  [31:0] Instruction,
  input  Fetch,
  input  Execute,
  output [3:0] Condition,
  output Halt,
  output [3:0] Reg_dest,
  output [3:0] Reg_B,
  output [3:0] Reg_A,
  output [2:0] Opcode,
  output nRE,
  output nWE,
  output [21:0] Constant,
  output SetFlags,
  output UseConstant
);

  wire and_1_out, and_2_out, not_1_out, not_2_out, or_1_out, xnor_1_out;
  wire [3:0] instructionpush_1_reg_a, instructionsplitter_1_reg_a, instructionwrite_1_p3;
  wire [9:0] instructionread_1_p2, instructionsplitter_1_constant, instructionwrite_1_p2;
  wire [21:0] bitextender_1_out, bitextender_2_out, bitextender_3_out, instructionloadhi_1_constant;

  InstructionSplitter instructionsplitter_1 (
    .Instruction(Instruction), .Opcode(Opcode), .SetFlags(SetFlags),
    .Constant(instructionsplitter_1_constant), .Reg_A(instructionsplitter_1_reg_a));  // open: Reg_B, Reg_dest, UseConstant
  InstructionLOADHI instructionloadhi_1 (
    .Instruction(Instruction), .Constant(instructionloadhi_1_constant));  // open: Reg_dest
  InstructionPOP instructionpop_1 (.Instruction(Instruction));  // open: Reg_dest
  InstructionPUSH instructionpush_1 (.Instruction(Instruction), .Reg_A(instructionpush_1_reg_a));
  // InstructionWRITE instructionwrite_1: pin names not known; wires that end beside it: Instruction, instructionwrite_1_p2, instructionwrite_1_p3
  // InstructionREAD instructionread_1: pin names not known; wires that end beside it: Instruction, instructionread_1_p2
  BitExtender #(.inputBits(10), .outputBits(22)) bitextender_1 (
    .in(instructionsplitter_1_constant), .out(bitextender_1_out));
  BitExtender #(.inputBits(10), .outputBits(22)) bitextender_2 (.in(instructionwrite_1_p2), .out(bitextender_2_out));
  BitExtender #(.inputBits(10), .outputBits(22)) bitextender_3 (.in(instructionread_1_p2), .out(bitextender_3_out));
  not not_1 (not_1_out, Instruction[30]);
  not not_2 (not_2_out, Instruction[31]);
  xnor xnor_1 (xnor_1_out, 1'b0, Instruction[26], Instruction[27], Instruction[28]);
  and and_1 (and_1_out, Instruction[30], Instruction[31]);
  or or_1 (or_1_out, not_1_out, not_2_out);
  and and_2 (and_2_out, xnor_1_out, and_1_out);
  or or_2 (UseConstant, and_2_out, or_1_out);
  Multiplexer #(.Bits(22), .Selector_Bits(3)) multiplexer_1 (
    .sel(Instruction[31:29]), .in_0(bitextender_1_out), .in_1(bitextender_1_out), .in_2(bitextender_1_out),
    .in_3(bitextender_1_out), .in_4(instructionloadhi_1_constant), .in_5(instructionloadhi_1_constant),
    .in_6(bitextender_2_out), .in_7(bitextender_3_out), .out(Constant));
  Multiplexer #(.Bits(4), .Selector_Bits(2)) multiplexer_2 (
    .sel({Instruction[31], Instruction[26]}), .in_0(4'b0000), .in_1(instructionsplitter_1_reg_a),
    .in_2(instructionwrite_1_p3), .in_3(instructionpush_1_reg_a), .out(Reg_A));
  AllBits1 allbits1_1 (.Instruction_NoCond(Instruction[31:4]), .AllBits1(Halt));

  assign Condition = Instruction[3:0];

  // Notes on the sheet:
  //   Instruction: The instruction machine code input. If the CPU is in the fetch phase and a rising clock signal occurs, this machine code is stored in the internal instruction register (IR), so that it can be decoded and executed.
  //   Condition: Instruction condition output, which contains the condition under which the instruction should be executed.
  //   Reg_dest: Destination register output, which determines the register that should store the result of a data operation. A data operation is either an ALU computation, or a read from an external device, such as RAM.
  //   Reg_B: B register output, which determines the register to be used for the second operand.
  //   Reg_A: A register output, which determines the register to be used for the first operand.
  //   Opcode: Opcode output, which determines the operation the ALU should perform.
endmodule
